// Digital circuit CU.dig as structural Verilog
module CU (
  input  A,
  input  B,
  input  C,
  input  D,
  output [1:0] RR2,
  output PC,
  output SLT,
  output AND,
  output [1:0] RR1,
  output XOR,
  output ADD,
  output SUB,
  output [1:0] WR,
  output WE,
  output IL,
  output OR
);

  wire and_7_out, and_8_out, and_9_out, and_10_out, not_1_out, not_2_out, not_3_out, not_4_out, not_5_out,
       not_6_out, not_7_out, not_8_out, not_9_out, not_10_out, not_11_out, or_2_out;

  not not_1 (not_1_out, D);
  not not_2 (not_2_out, C);
  not not_3 (not_3_out, B);
  not not_4 (not_4_out, C);
  not not_5 (not_5_out, D);
  not not_6 (not_6_out, A);
  not not_7 (not_7_out, B);
  not not_8 (not_8_out, B);
  not not_9 (not_9_out, D);
  not not_10 (not_10_out, A);
  not not_11 (not_11_out, D);
  not not_12 (RR1[0], A);
  and and_1 (PC, A, B, C, D);
  and and_2 (SLT, A, B, C, not_1_out);
  and and_3 (AND, A, B, C, D);
  and and_4 (XOR, A, B, not_2_out, D);
  and and_5 (ADD, A, not_3_out, not_4_out, D);
  and and_6 (SUB, A, B, C, not_5_out);
  and and_7 (and_7_out, not_6_out, not_7_out, C);
  and and_8 (and_8_out, A, not_8_out, not_9_out);
  or or_1 (WE, A, C, D);
  and and_9 (and_9_out, not_10_out, C);
  and and_10 (and_10_out, not_10_out, D);
  and and_11 (OR, A, B, C, not_11_out);
  or or_2 (or_2_out, and_7_out, and_8_out);
  or or_3 (IL, and_9_out, and_10_out);
  not not_13 (WR[0], or_2_out);

  assign RR1[1] = 1'b0;
  assign RR2 = 2'b01;
  assign WR[1] = 1'b0;
endmodule
