// Digital circuit InstructionRegister.dig as structural Verilog
module InstructionRegister (
  input  Clock,
  input  [1:0] En,
  input  [3:0] Op,
  output NOP,
  output MovA,
  output MovB,
  output MovA_B,
  output MovB_A,
  output AddA_B,
  output SubA_B,
  output AndA_B,
  output OrA_B,
  output XorA_B,
  output SLTA_B
);

  wire decoder_1_out_11;
  wire [3:0] _4bit_register_1_p4;

  Decoder #(.Selector_Bits(4)) decoder_1 (
    .sel(_4bit_register_1_p4), .out_0(NOP), .out_1(MovA), .out_2(MovB), .out_3(MovA_B), .out_4(MovB_A),
    .out_5(AddA_B), .out_6(SubA_B), .out_7(AndA_B), .out_8(OrA_B), .out_9(XorA_B), .out_10(SLTA_B),
    .out_11(decoder_1_out_11), .out_12(decoder_1_out_11), .out_13(decoder_1_out_11),
    .out_14(decoder_1_out_11), .out_15(decoder_1_out_11));
  // _4Bit_Register _4bit_register_1: pin names not known; wires that end beside it: Op, Clock, En, _4bit_register_1_p4
  // also tied to GND on the sheet: decoder_1_out_11
endmodule
