// Digital circuit ProgramCounter.dig as structural Verilog
module ProgramCounter (
  input  Clock,
  input  [1:0] En2,
  input  [3:0] Address,
  input  En1,
  output [3:0] Out
);

  wire [3:0] _4bit_fulladder_1_p4, multiplexer_1_out;

  Multiplexer #(.Bits(4)) multiplexer_1 (
    .sel(En1), .in_0(_4bit_fulladder_1_p4), .in_1(Address), .out(multiplexer_1_out));
  // _4Bit_Register _4bit_register_1: pin names not known; wires that end beside it: multiplexer_1_out, Clock, En2, Out
  // _4bit_fullAdder _4bit_fulladder_1: pin names not known; wires that end beside it: Out, 4'b0001, 1'b0, _4bit_fulladder_1_p4
endmodule
